# Fritzing sketch Untitled Sketch (saved by Fritzing 0.9.3b)
perfboards: 1

parts:
  LED1 = RGB LED (com. cathode, rgb) [package="5 mm [THT]"]
  LED2 = RGB LED (com. cathode, rgb) [package="5 mm [THT]"]  # not connected
  LED3 = RGB LED (com. cathode, rgb) [package="5 mm [THT]"]  # not connected
  LED4 = RGB LED (com. cathode, rgb) [package="5 mm [THT]"]  # not connected
  LED5 = RGB LED (com. cathode, rgb) [package="5 mm [THT]"]  # not connected
  LED6 = RGB LED (com. cathode, rgb) [package="5 mm [THT]"]  # not connected
  LED7 = RGB LED (com. cathode, rgb) [package="5 mm [THT]"]  # not connected
  LED8 = RGB LED (com. cathode, rgb) [package="5 mm [THT]"]  # not connected
  LED9 = RGB LED (com. cathode, rgb) [package="5 mm [THT]"]  # not connected
  LED10 = RGB LED (com. cathode, rgb) [package="5 mm [THT]"]
  LED11 = RGB LED (com. cathode, rgb) [package="5 mm [THT]"]
  LED12 = RGB LED (com. cathode, rgb) [package="5 mm [THT]"]
  LED13 = RGB LED (com. cathode, rgb) [package="5 mm [THT]"]
  LED14 = RGB LED (com. cathode, rgb) [package="5 mm [THT]"]
  LED15 = RGB LED (com. cathode, rgb) [package="5 mm [THT]"]
  Raspberry_Pi_1 = Raspberry Pi 3 [part_number=RPI-3-V1.2]
  RE1 = Rotary Encoder [package=THT]  # not connected
  IC1 = MCP23017 I2C I/O Expander  # not connected
  IC2 = MCP23017 I2C I/O Expander  # not connected
  IC3 = MCP23017 I2C I/O Expander
  IC4 = MCP23017 I2C I/O Expander
  OLED_I2C1 = OLED 128x64 I2C Monochrome Display  # not connected
  S16 = Tactile Switch Buttons - 12mm Square [package=tactile-pth-12mm]
  S17 = Tactile Switch Buttons - 12mm Square [package=tactile-pth-12mm]
  S18 = Tactile Switch Buttons - 12mm Square [package=tactile-pth-12mm]
  S19 = Tactile Switch Buttons - 12mm Square [package=tactile-pth-12mm]
  S20 = Tactile Switch Buttons - 12mm Square [package=tactile-pth-12mm]
  S21 = Tactile Switch Buttons - 12mm Square [package=tactile-pth-12mm]
  S22 = Tactile Switch Buttons - 12mm Square [package=tactile-pth-12mm]
  S23 = Tactile Switch Buttons - 12mm Square [package=tactile-pth-12mm]
  S24 = Tactile Switch Buttons - 12mm Square [package=tactile-pth-12mm]
  S25 = Tactile Switch Buttons - 12mm Square [package=tactile-pth-12mm]
  S26 = Tactile Switch Buttons - 12mm Square [package=tactile-pth-12mm]
  S27 = Tactile Switch Buttons - 12mm Square [package=tactile-pth-12mm]
  S28 = Tactile Switch Buttons - 12mm Square [package=tactile-pth-12mm]
  S29 = Tactile Switch Buttons - 12mm Square [package=tactile-pth-12mm]
  S30 = Tactile Switch Buttons - 12mm Square [package=tactile-pth-12mm]

nets:
  N1: LED1.green_anode, IC4.GPA4
  N2: LED1.blue_anode, IC4.GPA5
  N3: LED10.green_anode, IC4.GPA6
  N4: LED10.blue_anode, IC4.GPA7
  N5: LED11.green_anode, IC4.A0
  N6: LED12.green_anode, IC4.A2
  N7: LED12.blue_anode, IC4.RESET
  N8: LED13.green_anode, IC4.INTB
  N9: LED13.blue_anode, IC4.INTA
  N10: LED14.green_anode, IC4.GPA0
  N11: LED14.blue_anode, IC4.GPA1
  N12: LED15.green_anode, IC4.GPA2
  N13: LED15.blue_anode, IC4.GPA3
  3V3: Raspberry_Pi_1.3v3, IC3.VDD
  N14: Raspberry_Pi_1.GPIO2, IC4.SDA
  N15: Raspberry_Pi_1.GPIO3, IC3.SCL
  N16: IC3.VSS, S29.2, S29.4
  N17: S16.1, S16.3
  N18: S16.2, S16.4
  N19: S17.1, S17.3
  N20: S17.2, S17.4
  N21: S18.1, S18.3
  N22: S18.2, S18.4
  N23: S19.1, S19.3
  N24: S19.2, S19.4
  N25: S20.1, S20.3
  N26: S20.2, S20.4
  N27: S21.1, S21.3
  N28: S21.2, S21.4
  N29: S22.1, S22.3
  N30: S22.2, S22.4
  N31: S23.1, S23.3
  N32: S23.2, S23.4
  N33: S24.1, S24.3
  N34: S24.2, S24.4
  N35: S25.1, S25.3
  N36: S25.2, S25.4
  N37: S26.1, S26.3
  N38: S26.2, S26.4
  N39: S27.1, S27.3
  N40: S27.2, S27.4
  N41: S28.1, S28.3
  N42: S28.2, S28.4
  N43: S29.1, S29.3
  N44: S30.1, S30.3
  N45: S30.2, S30.4

custom parts:
  MCP23017 I2C I/O Expander: The MCP23017 uses two i2c pins (these can be shared with other i2c devices), and in exchange gives you 16 general purpose pins. You can set each of 16 pins to be input, output, input with a pullup or open drain. There's even the ability to get an interrupt via an external pin when any of the inputs change so you don't have to keep polling the chip.
  Tactile Switch Buttons - 12mm Square: Medium-sized clicky momentary switches are standard input "buttons" on electronic projects. These work best in a PCB but can be used on a solderless breadboard as shown in this tutorial. The pins are normally open (disconnected) and when the button is pressed they are momentarily closed. They come in a pack of 10, they're pretty handy so you'll want to keep them around. You can find an EAGLE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
